// Logisim project RISC-MC8_Computer.circ as structural Verilog: 8 circuits, main circuit main
module main (
);

  wire alu_1_zero, and_1_out, Clk_out, Clr_out, control_1_copyreg, control_1_iregdest, control_1_jump,
       control_1_memread, control_1_memwrite, control_1_regwrite, control_1_setimm, control_1_setimmhigh,
       control_1_tryskip, not_1_out, or_1_out;
  wire [2:0] control_1_aluop, multiplexer_2_out, splitinstruction_1_regop;
  wire [3:0] splitinstruction_1_setimm;
  wire [4:0] splitinstruction_1_opcode;
  wire [7:0] adder_1_out, alu_1_aluout, DataMemory_dout, immset_1_iregoutput, InstructionMemory_data,
       multiplexer_1_out, multiplexer_3_out, multiplexer_4_out, multiplexer_5_out, multiplexer_6_out, PC_q,
       registerfile_1_iregdata, registerfile_1_readdata, splitinstruction_1_jumpoffset;

  Register #(.trigger("falling")) PC (.D(adder_1_out), .en(1'b1), .clk(Clk_out), .Q(PC_q), .clr(Clr_out));
  Clock Clk (.out(Clk_out));
  Multiplexer #(.width(8)) multiplexer_1 (
    .in0(8'h1), .in1(splitinstruction_1_jumpoffset), .out(multiplexer_1_out), .sel(control_1_jump));
  ROM InstructionMemory (.addr(PC_q), .data(InstructionMemory_data));
  Button Clr (.out(Clr_out));
  and and_1 (and_1_out, control_1_tryskip, alu_1_zero);
  Adder adder_1 (.a(multiplexer_1_out), .b(PC_q), .out(adder_1_out), .cin(and_1_out));  // open: cout
  SplitInstruction splitinstruction_1 (
    .Instruction(InstructionMemory_data), .SetImm(splitinstruction_1_setimm),
    .JumpOffset(splitinstruction_1_jumpoffset), .Opcode(splitinstruction_1_opcode),
    .RegOp(splitinstruction_1_regop));
  Multiplexer #(.width(3)) multiplexer_2 (
    .in0(splitinstruction_1_regop), .in1(3'b000), .out(multiplexer_2_out), .sel(control_1_iregdest));
  not not_1 (not_1_out, Clk_out);
  Control control_1 (
    .Opcode(splitinstruction_1_opcode), .Jump(control_1_jump), .ALUop(control_1_aluop),
    .MemRead(control_1_memread), .MemWrite(control_1_memwrite), .RegWrite(control_1_regwrite),
    .iRegDest(control_1_iregdest), .SetImm(control_1_setimm), .SetImmHigh(control_1_setimmhigh),
    .CopyReg(control_1_copyreg), .TrySkip(control_1_tryskip));
  RegisterFile registerfile_1 (
    .WriteEnable(control_1_regwrite), .ReadReg(splitinstruction_1_regop), .WriteData(multiplexer_6_out),
    .WriteReg(multiplexer_2_out), .Clock(not_1_out), .Clear(Clr_out), .iRegData(registerfile_1_iregdata),
    .ReadData(registerfile_1_readdata));
  RAM DataMemory (
    .addr(registerfile_1_iregdata), .we(control_1_memwrite), .oe(control_1_memread), .clk(Clk_out),
    .din(registerfile_1_readdata), .dout(DataMemory_dout));
  Multiplexer #(.width(8)) multiplexer_3 (
    .in0(registerfile_1_iregdata), .in1(registerfile_1_readdata), .out(multiplexer_3_out),
    .sel(control_1_iregdest));
  ImmSet immset_1 (
    .SetHigh(control_1_setimmhigh), .Immediate(splitinstruction_1_setimm),
    .iRegInput(registerfile_1_iregdata), .iRegOutput(immset_1_iregoutput));
  ALU alu_1 (
    .ALUop(control_1_aluop), .iRegInput(registerfile_1_iregdata), .RegInput(registerfile_1_readdata),
    .Zero(alu_1_zero), .ALUout(alu_1_aluout));
  Multiplexer #(.width(8)) multiplexer_4 (
    .in0(multiplexer_3_out), .in1(immset_1_iregoutput), .out(multiplexer_4_out), .sel(control_1_setimm));
  or or_1 (or_1_out, control_1_setimm, control_1_copyreg);
  Multiplexer #(.width(8)) multiplexer_5 (
    .in0(alu_1_aluout), .in1(multiplexer_4_out), .out(multiplexer_5_out), .sel(or_1_out));
  Multiplexer #(.width(8)) multiplexer_6 (
    .in0(multiplexer_5_out), .in1(DataMemory_dout), .out(multiplexer_6_out), .sel(control_1_memread));

  // Notes on the sheet:
  //   contents of InstructionMemory (hex, n*v repeats v):
  //   6f 71 31 28 39 32 60 2 5a 37 8 33 70 62 1b 34 61 24 4a 45 68 36 62 56 6b 56 83 37 58 ff 80
endmodule

module RegisterFile (
  input  WriteEnable,
  input  [2:0] ReadReg,
  input  [7:0] WriteData,
  input  [2:0] WriteReg,
  input  Clock,
  input  Clear,
  output [7:0] iRegData,
  output [7:0] ReadData
);

  wire demultiplexer_1_out0, demultiplexer_1_out1, demultiplexer_1_out2, demultiplexer_1_out3,
       demultiplexer_1_out4, demultiplexer_1_out5, demultiplexer_1_out6, demultiplexer_1_out7;
  wire [7:0] r1_q, r2_q, r3_q, r4_q, r5_q, r6_q, r7_q;

  Demultiplexer #(.select(3)) demultiplexer_1 (
    .out0(demultiplexer_1_out0), .out1(demultiplexer_1_out1), .out2(demultiplexer_1_out2),
    .out3(demultiplexer_1_out3), .out4(demultiplexer_1_out4), .out5(demultiplexer_1_out5),
    .out6(demultiplexer_1_out6), .out7(demultiplexer_1_out7), .in(WriteEnable), .sel(WriteReg));
  Register ireg (.D(WriteData), .en(demultiplexer_1_out0), .clk(Clock), .Q(iRegData), .clr(Clear));
  Register r1 (.D(WriteData), .en(demultiplexer_1_out1), .clk(Clock), .Q(r1_q), .clr(Clear));
  Register r2 (.D(WriteData), .en(demultiplexer_1_out2), .clk(Clock), .Q(r2_q), .clr(Clear));
  Register r3 (.D(WriteData), .en(demultiplexer_1_out3), .clk(Clock), .Q(r3_q), .clr(Clear));
  Register r4 (.D(WriteData), .en(demultiplexer_1_out4), .clk(Clock), .Q(r4_q), .clr(Clear));
  Register r5 (.D(WriteData), .en(demultiplexer_1_out5), .clk(Clock), .Q(r5_q), .clr(Clear));
  Register r6 (.D(WriteData), .en(demultiplexer_1_out6), .clk(Clock), .Q(r6_q), .clr(Clear));
  Register r7 (.D(WriteData), .en(demultiplexer_1_out7), .clk(Clock), .Q(r7_q), .clr(Clear));
  Multiplexer #(.select(3), .width(8)) multiplexer_1 (
    .in0(iRegData), .in1(r1_q), .in2(r2_q), .in3(r3_q), .in4(r4_q), .in5(r5_q), .in6(r6_q), .in7(r7_q),
    .out(ReadData), .sel(ReadReg));
endmodule

module DataMemory (
  input  [7:0] Address,
  input  WriteEnable,
  input  [7:0] WriteData,
  input  Clock,
  output [7:0] ReadData
);

  RAM ram_1 (.addr(Address), .we(WriteEnable), .oe(1'b1), .clk(Clock), .din(WriteData), .dout(ReadData));
endmodule

module SplitInstruction (
  input  [7:0] Instruction,
  output [4:0] Opcode,
  output [2:0] RegOp,
  output [3:0] SetImm,
  output [7:0] JumpOffset
);


  assign JumpOffset = {{2{Instruction[6]}}, Instruction[5:0]};
  assign Opcode = Instruction[7:3];
  assign RegOp = Instruction[2:0];
  assign SetImm = Instruction[3:0];

  // Notes on the sheet:
  //   sign extend 7 -> 8 bit
endmodule

module Control (
  input  [4:0] Opcode,
  output Jump,
  output [2:0] ALUop,
  output MemRead,
  output MemWrite,
  output RegWrite,
  output iRegDest,
  output SetImm,
  output SetImmHigh,
  output CopyReg,
  output TrySkip
);

  wire ADD_SUB_out, DUPR_out, NOT_STOR_SKIP_JUMP_out, OR_XOR_out, SHIFT2_out, SHIFT_out, SKIP_out;

  and LOAD (MemRead, ~Opcode[0], ~Opcode[1], ~Opcode[2], Opcode[3], ~Opcode[4]);  // AND_Gate
  and STOR (MemWrite, Opcode[0], ~Opcode[1], ~Opcode[2], Opcode[3], ~Opcode[4]);  // AND_Gate
  nand NOT_STOR_SKIP_JUMP (NOT_STOR_SKIP_JUMP_out, Opcode[0], ~Opcode[2], Opcode[3], ~Opcode[4]);  // NAND_Gate
  and DUPR (DUPR_out, Opcode[0], Opcode[1], Opcode[2], ~Opcode[3], ~Opcode[4]);  // AND_Gate
  and STLO_STHI (SetImm, Opcode[2], Opcode[3], ~Opcode[4]);  // AND_Gate
  and DUPI_DUPR (CopyReg, Opcode[1], Opcode[2], ~Opcode[3], ~Opcode[4]);  // AND_Gate
  and and_1 (TrySkip, Opcode[0], Opcode[1], ~Opcode[2], Opcode[3], ~Opcode[4]);  // AND_Gate
  and OR_XOR (OR_XOR_out, ~Opcode[1], Opcode[2], ~Opcode[3]);  // AND_Gate
  and SHIFT (SHIFT_out, ~Opcode[0], Opcode[1], ~Opcode[2], Opcode[3]);  // AND_Gate
  and ADD_SUB (ADD_SUB_out, Opcode[1], ~Opcode[2], ~Opcode[3]);  // AND_Gate
  and SHIFT2 (SHIFT2_out, ~Opcode[0], Opcode[1], ~Opcode[2], Opcode[3]);  // AND_Gate
  and SKIP (SKIP_out, Opcode[0], Opcode[1], ~Opcode[2], Opcode[3]);  // AND_Gate
  and and_2 (RegWrite, NOT_STOR_SKIP_JUMP_out, ~Opcode[4]);  // AND_Gate
  or or_1 (iRegDest, DUPR_out, SetImm);
  or or_2 (ALUop[2], OR_XOR_out, SHIFT_out);
  or or_3 (ALUop[1], ADD_SUB_out, SHIFT2_out, SKIP_out);

  assign ALUop[0] = Opcode[0];
  assign Jump = Opcode[4];
  assign SetImmHigh = Opcode[1];
endmodule

module ALU (
  input  [2:0] ALUop,
  input  [7:0] iRegInput,
  input  [7:0] RegInput,
  output Zero,
  output [7:0] ALUout
);

  wire [7:0] adder_1_out, and_1_out, multiplexer_1_out, nand_1_out, not_1_out, or_1_out,
       shift_1_shiftedvalue, xor_1_out;

  assign and_1_out = iRegInput & RegInput;  // AND_Gate and_1, 8 bits wide
  assign nand_1_out = ~(RegInput & iRegInput);  // NAND_Gate nand_1, 8 bits wide
  Multiplexer #(.width(8)) multiplexer_1 (.in0(iRegInput), .in1(not_1_out), .out(multiplexer_1_out), .sel(ALUop[0]));
  assign not_1_out = ~iRegInput;  // NOT_Gate not_1, 8 bits wide
  assign or_1_out = RegInput | iRegInput;  // OR_Gate or_1, 8 bits wide
  assign xor_1_out = RegInput ^ iRegInput;  // XOR_Gate xor_1, 8 bits wide
  Adder adder_1 (.a(RegInput), .b(multiplexer_1_out), .out(adder_1_out), .cin(ALUop[0]));  // open: cout
  Multiplexer #(.select(3), .width(8)) multiplexer_2 (
    .in0(and_1_out), .in1(nand_1_out), .in2(adder_1_out), .in3(adder_1_out), .in4(or_1_out), .in5(xor_1_out),
    .in6(shift_1_shiftedvalue), .out(ALUout), .sel(ALUop));  // open: in7
  Shift shift_1 (.Value(RegInput), .ShiftAmount(iRegInput[3:0]), .ShiftedValue(shift_1_shiftedvalue));
  nor nor_1 (Zero, ALUout[0], ALUout[1], ALUout[2], ALUout[3], ALUout[4], ALUout[5], ALUout[6], ALUout[7]);
endmodule

module ImmSet (
  input  SetHigh,
  input  [3:0] Immediate,
  input  [7:0] iRegInput,
  output [7:0] iRegOutput
);

  wire not_1_out;

  not not_1 (not_1_out, SetHigh);
  Multiplexer #(.width(8)) multiplexer_1 (
    .in0({Immediate, iRegInput[3:0]}), .in1({iRegInput[7:4], Immediate}), .out(iRegOutput), .sel(not_1_out));
endmodule

module Shift (
  input  [7:0] Value,
  input  [3:0] ShiftAmount,
  output [7:0] ShiftedValue
);

  wire and_1_out, not_1_out, not_2_out, xor_1_out, xor_2_out;
  wire [7:0] multiplexer_1_out, multiplexer_2_out, multiplexer_4_out, shifter_1_out;

  Shifter shifter_1 (.in(Value), .\dist (ShiftAmount[2:0]), .out(shifter_1_out));
  not not_1 (not_1_out, ShiftAmount[0]);
  not not_2 (not_2_out, ShiftAmount[1]);
  Multiplexer #(.width(8)) multiplexer_1 (
    .in0({1'b0, Value[7:1]}), .in1(Value), .out(multiplexer_1_out), .sel(not_1_out));
  xor xor_1 (xor_1_out, ShiftAmount[1], not_1_out);
  and and_1 (and_1_out, not_1_out, not_2_out);
  Multiplexer #(.width(8)) multiplexer_2 (
    .in0({2'b00, multiplexer_1_out[7:2]}), .in1(multiplexer_1_out), .out(multiplexer_2_out), .sel(xor_1_out));
  xor xor_2 (xor_2_out, and_1_out, ShiftAmount[2]);
  Multiplexer #(.width(8)) multiplexer_3 (
    .in0(shifter_1_out), .in1(multiplexer_4_out), .out(ShiftedValue), .sel(ShiftAmount[3]));
  Multiplexer #(.width(8)) multiplexer_4 (
    .in0({4'b0000, multiplexer_2_out[7:4]}), .in1(multiplexer_2_out), .out(multiplexer_4_out), .sel(xor_2_out));
endmodule
